# Fritzing sketch schematic_lcd_base (saved by Fritzing 0.9.3b)
breadboards: 1

parts:
  LCD1 = LCD screen  # not connected
  Part1 = Arduino Uno (Rev3)
  R1 = Resistor [tolerance=±5% resistance=220 package="2512 [SMD]"]
  R2 = Rotary Potentiometer (Small) [maximum_resistance=100kΩ package=THT]  # not connected
  LED1 = smd LED [color="Red (633nm)" package="0805 [SMD]"]
  LED2 = smd LED [color="Orange (605nm)" package="0805 [SMD]"]
  LED3 = smd LED [color="Green (555nm)" package="0805 [SMD]"]
  J1 = Piezo Speaker
  HC-SR04_Sensor_1 = HC-SR04 Ultrasonic Distance Sensor
  R3 = Resistor [tolerance=±5% resistance=220 package="0805 [SMD]"]
  R4 = Resistor [tolerance=±5% resistance=220 package="0805 [SMD]"]
  R5 = Resistor [tolerance=±5% resistance=220 package="0805 [SMD]"]

nets:
  N1: Part1.D8, LED3.cathode
  N2: Part1.D9_PWM, HC-SR04_Sensor_1.TRIG, HC-SR04_Sensor_1.ECHO
  N3: Part1.D10_PWM/SS, J1.pin2
  GND: Part1.GND, J1.pin1, HC-SR04_Sensor_1.GND, R3.Pin_0, R4.Pin_0, R5.Pin_0
  N4: Part1.D6_PWM, LED1.cathode
  N5: Part1.D7, LED2.cathode
  5V: Part1.5V, R1.Pin_0, HC-SR04_Sensor_1.VCC
  N6: LED1.anode, R3.Pin_1
  N7: LED2.anode, R4.Pin_1
  N8: LED3.anode, R5.Pin_1
